// Logisim project 2_1.circ as structural Verilog: 5 circuits, main circuit aufgabe1
module aufgabe1 (
  input  A,
  input  B,
  output out_3,
  output out_4
);

  wire not_1_out, not_2_out;

  not not_1 (not_1_out, B);
  not not_2 (not_2_out, A);
  or or_1 (out_4, not_1_out, not_2_out);
  nand nand_1 (out_3, A, B);

  // Notes on the sheet:
  //   Aufgabe 1
endmodule

module lecture (
  input  A,
  input  B,
  input  A_2,
  input  B_2,
  input  C,
  input  D,
  input  E,
  output out_8,
  output out_9
);

  wire and_1_out, and_2_out, and_3_out, nand_1_out, not_1_out, not_2_out, or_2_out;

  not not_1 (not_1_out, A);
  not not_2 (not_2_out, B);
  and and_1 (and_1_out, not_1_out, B);
  and and_2 (and_2_out, A, not_2_out);
  and and_3 (and_3_out, A_2, ~B_2);  // AND_Gate
  nand nand_1 (nand_1_out, C, D, E);
  or or_1 (out_8, and_1_out, and_2_out);
  not not_3 (out_9, or_2_out);
  or or_2 (or_2_out, and_3_out, nand_1_out);

  // Notes on the sheet:
  //   Aufgabe von Seite 6: EXOR mittels AND, OR, NOT darstellen
  //   Aufgabe von Seite 8:
endmodule

module aufgabe3 (
  input  V,
  input  U,
  input  W,
  output out_4
);

  wire and_1_out, and_2_out, and_3_out;

  and and_1 (and_1_out, ~V, ~U, W);  // AND_Gate
  and and_2 (and_2_out, V, ~U, ~W);  // AND_Gate
  and and_3 (and_3_out, ~V, U, W);  // AND_Gate
  or or_1 (out_4, and_1_out, and_2_out, and_3_out);

  // Notes on the sheet:
  //   Aufgabe 3
endmodule

module aufgabe3_1 (
  input  V,
  input  U,
  input  W,
  output x
);

  wire and_1_out, and_2_out, not_1_out, not_2_out, not_3_out;

  not not_1 (not_1_out, V);
  not not_2 (not_2_out, U);
  not not_3 (not_3_out, W);
  and and_1 (and_1_out, not_1_out, W);
  and and_2 (and_2_out, V, not_2_out, not_3_out);
  or or_1 (x, and_1_out, and_2_out);

  // Notes on the sheet:
  //   optimized via aufgabe3
endmodule

module aufgabe4 (
  input  A,
  input  B,
  input  C,
  input  B_2,
  input  C_2,
  input  A_2,
  output out_7,
  output out_8
);

  wire nor_1_out, nor_2_out;

  nor nor_1 (nor_1_out, A, B);
  nor nor_2 (nor_2_out, B_2, C_2);
  nor nor_3 (out_7, nor_1_out, C);
  nor nor_4 (out_8, nor_2_out, A_2);

  // Notes on the sheet:
  //   Aufgabe 4 / Assoziation bei nors
endmodule
